// Logisim project hw1.circ as structural Verilog: 1 circuit, main circuit main
module main (
);

  wire transistor_1_out, transmission_1_p1, transmission_1_p2, transmission_1_p6, transmission_2_p3,
       transmission_2_p4;
  wire [1:0] multiplexer_1_out, undriven;

  // Transmission_Gate transmission_1: pin names not known; wires that end beside it: transmission_1_p1, transmission_1_p2, transmission_1_p1, transmission_1_p2, 1'b1, transmission_1_p6, transmission_1_p1, transmission_1_p1, transmission_1_p1
  // Transmission_Gate #(.gate("br")) transmission_2: pin names not known; wires that end beside it: 1'b1, transmission_1_p6, transmission_2_p3, transmission_2_p4, transmission_2_p3, transmission_2_p4, transmission_1_p6, transmission_2_p3, transmission_2_p3
  Transistor #(.\type ("n"), .gate("br")) transistor_1 (.in(transmission_1_p6), .out(transistor_1_out));  // open: gate
  Transistor #(.\type ("n"), .gate("br")) transistor_2 (.in(transistor_1_out), .out(transmission_1_p6));  // open: gate
  Multiplexer #(.width(2)) multiplexer_1 (
    .in0(undriven), .out(multiplexer_1_out), .sel(transmission_2_p3), .en(transmission_1_p1));  // open: in1
  // also tied to GND on the sheet: transmission_1_p6

  // Notes on the sheet:
  //   Y'
  //   B[3]
  //   Cout3
  //   FA
  //   S[3]
  //   B[2]
  //   A[3]
  //   Cout2
  //   FA
  //   S[2]
  //   1
  //   A[2]
  //   B[3]
  //   FA
  //   S[3]
  //   S[3:2], overflow
  //   X'
  //   f
  //   X'
  //   Y'
  //   A[3]
  //   B[2]
  //   Cout2
  //   FA
  //   S[2]
  //   A[2]
  //   0
  //   B[1]
  //   Cout1
  //   A[1]
  //   Cout0
  //   FA
  //   S[1]
  //   A[0]
  //   B[0]
  //   FA
  //   S[0]
  //   0
endmodule
